# Fritzing sketch BALtiny (saved by Fritzing 0.9.3b)
breadboards: 1

parts:
  U1 = ATTINY45 [package=dip]
  R1 = Resistor [tolerance=±5% resistance=220 package="0603 [SMD]"]
  R2 = Resistor [tolerance=±5% resistance=220 package="0603 [SMD]"]
  LED1 = LED - 5mm [color="Red (633nm)" package="5 mm [THT]"]
  S2 = Momentary Switch [package=ksa_sealed_tac_switch]
  R3 = Resistor [tolerance=±5% resistance=220 package="0603 [SMD]"]
  R4 = PHOTOCELL [package=photocell-kit]

nets:
  N1: U1.PB4(ADC2), R1.Pin_1, R4.P$2
  N2: U1.GND, R1.Pin_0, R2.Pin_0, R3.Pin_0
  N3: U1.PB0(MOSI), LED1.anode
  N4: U1.PB1(MISO), S2.2, R3.Pin_1
  N5: U1.VCC, S2.4, R4.P$1
  N6: R2.Pin_1, LED1.cathode
